# Fritzing sketch Trasmit-Receive (saved by Fritzing 0.8.7b)

parts:
  U4 = LCD-16X2 [package=lcd-16x2]
  R3 = Trimmer Potentiometer [maximum_resistance=10kΩ package=THT]
  R4 = Resistor [tolerance=±5% resistance=220 package=THT]
  433Mhz_TR1 = mystery part, 3 pins [chip_label=?]
  433Mhz_RX1 = mystery part, 4 pins [chip_label=?]
  Bluno_Beetle2 = Bluno Beetle [part_number=BlunoBeetle]
  Εξάρτημα5 = Arduino Nano (Rev3.0)
  BAT2 = Battery Holders [package=battcom_20mm_pth]
  VCC2 = Battery block 9V
  S6 = Pushbutton [package="[THT]"]

nets:
  N1: U4.VO, R3.wiper
  N2: U4.RS, Εξάρτημα5.D12/MISO
  N3: U4.E, Εξάρτημα5.D11/MOSI
  N4: U4.DB4, Εξάρτημα5.D9
  N5: U4.DB5, Εξάρτημα5.D8
  N6: U4.DB6, Εξάρτημα5.D7
  N7: U4.DB7, Εξάρτημα5.D6
  N8: U4.A, R4.Pin_0
  N9: 433Mhz_TR1.pin1, Bluno_Beetle2.A3, Bluno_Beetle2.5V
  N10: 433Mhz_TR1.pin2, Bluno_Beetle2.D5
  GND: 433Mhz_TR1.pin3, Bluno_Beetle2.GND, Bluno_Beetle2.VIN, BAT2.+, BAT2.-, S6.Pin_3, S6.Pin_4
  N11: 433Mhz_RX1.pin1, Εξάρτημα5.5V
  N12: 433Mhz_RX1.pin3, Εξάρτημα5.D4
  N13: 433Mhz_RX1.pin4, Εξάρτημα5.GND, VCC2.-
  N14: Εξάρτημα5.VIN, VCC2.+

custom parts:
  Bluno Beetle: DF Robot Bluno Beetle. BLE Bluetooth Arduino.
