# Fritzing sketch Mikroi-Diasostes-v6 (saved by Fritzing 0.8.7b)

parts:
  S1 = KY-026
  S2 = KY-026
  S3 = KY-026
  FIRE_SENSOR = KY-026
  TEMPRETURE_SENSOR = Humidity and Temperature Sensor DHT11  # not connected
  RELAY = 4-Channel 5v Relay Shield [package=relay-4ch5v10a]
  GAS_SENSOR = MQ-7 breakout
  RAIN_SENSOR = YL-83 Rain Sensor - Detection Board
  YL-83_-_Control_Board1 = YL-83 Rain Sensor - Control Board
  EARTHQUAKE_SENSOR = MPU-6050 Board GY-521 [form="♀ (female)" package=THT]
  LCD = LCD-16X2 [package=lcd-16x2_noholes]
  LCM1602_IIC1 = LCM1602 IIC [part_number="LCM1602 IIC" chip_label="LCM1602 IIC" package="DIP (Dual Inline) [THT]"]
  Εξάρτημα3 = Arduino Mega ADK (Rev3)
  433Mhz_TR = mystery part, 3 pins [chip_label=?]
  433Mhz_RX = mystery part, 4 pins [chip_label=?]
  Bluno_Beetle1 = Bluno Beetle [part_number=BlunoBeetle]
  Εξάρτημα4 = Arduino Nano (Rev3.0)
  BAT1 = Battery Holders [package=battcom_20mm_pth]
  VCC1 = Battery block 9V
  VCC2 = Battery block 9V
  S5 = Pushbutton [package="[THT]"]
  S6 = KY-026
  LCD_2 = LCD-16X2 [package=lcd-16x2]
  R1 = Trimmer Potentiometer [maximum_resistance=10kΩ package=THT]
  R2 = Resistor [tolerance=±5% resistance=220 package=THT]
  BUZZER = Piezo Speaker  # not connected
  U4 = mystery part, 3 pins [chip_label=?]
  U5 = mystery part, 3 pins [chip_label=?]
  S7 = Pushbutton [package="[THT]"]
  TSOUNAMI_SENSOR_(FLOTER)_ON/OFF_SWITCH = mystery part, 3 pins [chip_label=?]

nets:
  N1: S1.pin1, Εξάρτημα3.A3
  N2: S2.pin1, Εξάρτημα3.A2
  N3: S3.pin1, Εξάρτημα3.A1
  N4: FIRE_SENSOR.pin1, Εξάρτημα3.A0
  N5: RELAY.IN1, Εξάρτημα3.D33
  N6: RELAY.IN2, Εξάρτημα3.D35
  N7: RELAY.IN4, Εξάρτημα3.D39
  N8: RELAY.IN3, Εξάρτημα3.D37
  VCC: GAS_SENSOR.VCC, Εξάρτημα3.3V3
  N9: GAS_SENSOR.DO, Εξάρτημα3.A7
  N10: RAIN_SENSOR.POS, YL-83_-_Control_Board1.POS
  N11: RAIN_SENSOR.NEG, YL-83_-_Control_Board1.NEG
  N12: EARTHQUAKE_SENSOR.pin1, Εξάρτημα3.5V
  VSS: LCD.VSS, LCM1602_IIC1.VSS
  VDD: LCD.VDD, LCM1602_IIC1.VDD
  N13: LCD.VO, LCM1602_IIC1.V0
  N14: LCD.RS, LCM1602_IIC1.RS
  N15: LCD.R_W, LCM1602_IIC1.RW
  N16: LCD.E, LCM1602_IIC1.E
  N17: LCD.DB0, LCM1602_IIC1.D0
  N18: LCD.DB1, LCM1602_IIC1.D1
  N19: LCD.DB2, LCM1602_IIC1.D2
  N20: LCD.DB3, LCM1602_IIC1.D3
  N21: LCD.DB4, LCM1602_IIC1.D4
  N22: LCD.DB5, LCM1602_IIC1.D5
  N23: LCD.DB6, LCM1602_IIC1.D6
  N24: LCD.DB7, LCM1602_IIC1.D7
  N25: LCD.A, LCM1602_IIC1.A
  N26: LCD.K, LCM1602_IIC1.K
  N27: LCM1602_IIC1.SDA, Εξάρτημα3.D20/SDA
  N28: LCM1602_IIC1.SCL, Εξάρτημα3.D21/SCL
  N29: Εξάρτημα3.A4, S6.pin1
  N30: Εξάρτημα3.GND, Εξάρτημα3.D2_PWM, VCC2.-, S7.Pin_1, S7.Pin_2
  N31: Εξάρτημα3.D8_PWM, U4.pin2
  N32: Εξάρτημα3.VIN, VCC2.+
  N33: Εξάρτημα3.D3_PWM, TSOUNAMI_SENSOR_(FLOTER)_ON/OFF_SWITCH.pin1
  N34: Εξάρτημα3.D6_PWM, U5.pin1
  N35: 433Mhz_TR.pin1, Bluno_Beetle1.A3, Bluno_Beetle1.5V
  N36: 433Mhz_TR.pin2, Bluno_Beetle1.D5
  GND: 433Mhz_TR.pin3, Bluno_Beetle1.GND, Bluno_Beetle1.VIN, BAT1.+, BAT1.-, S5.Pin_3, S5.Pin_4
  N37: 433Mhz_RX.pin1, Εξάρτημα4.5V
  N38: 433Mhz_RX.pin3, Εξάρτημα4.D4
  N39: 433Mhz_RX.pin4, Εξάρτημα4.GND, VCC1.-
  N40: Εξάρτημα4.D6, LCD_2.DB7
  N41: Εξάρτημα4.D7, LCD_2.DB6
  N42: Εξάρτημα4.D8, LCD_2.DB5
  N43: Εξάρτημα4.D9, LCD_2.DB4
  N44: Εξάρτημα4.D11/MOSI, LCD_2.E
  N45: Εξάρτημα4.D12/MISO, LCD_2.RS
  N46: Εξάρτημα4.VIN, VCC1.+
  N47: LCD_2.VO, R1.wiper
  N48: LCD_2.A, R2.Pin_0

custom parts:
  KY-026: ky-026 flame sensor module
  Humidity and Temperature Sensor DHT11: Digital relative humidity & temperature sensor DHT11
  4-Channel 5v Relay Shield: 4 Channel 5v Relay Shield w. 2x SPD-06VDC-SD-C
  MQ-7 breakout: MQ-5 gas sensor
  YL-83 Rain Sensor - Detection Board: The YL-83 is a rain sensor that has more resistance when dry and less resistance when wet. The module runs at 5V.
  YL-83 Rain Sensor - Control Board: The YL-83 is a rain sensor that has more resistance when dry and less resistance when wet. The module runs at 5V.
  MPU-6050 Board GY-521: Acelerometro y Giroscopio MPU-6050 Board GY-521
  LCM1602 IIC: I2C-Module to use a 1602 or 2004 LCD on with the wire.h libory Serial LCD Modul
  Bluno Beetle: DF Robot Bluno Beetle. BLE Bluetooth Arduino.
